# Fritzing sketch WRO2025 (saved by Fritzing 0.9.3b)
circuit board: 8.51115cm x 4.5101cm
breadboards: 2

parts:
  M2 = DC Motor
  IC1 = L293D [package=THT]
  Componente1 = Arduino Nano (Rev3.0)
  Componente2 = Arduino Uno (Rev3)
  hc-sr2 = hc-sr04
  J1 = Basic Servo
  VCC1 = Battery
  VCC2 = Battery

nets:
  N1: M2.pin_1, IC1.Out_1_(_Controlled_by_Enable_1_)
  N2: M2.pin_2, IC1.Out_2_(_Controlled_by_Enable_1_)
  N3: IC1.Enable_1, Componente1.D10
  N4: IC1.In_1, Componente1.D2
  N5: IC1.0V, Componente1.GND, VCC1.-
  N6: IC1.In_2, Componente1.D3
  N7: IC1.+Vmotor, IC1.Enable_2, Componente1.D11/MOSI, VCC1.+
  N8: IC1.In_3, Componente1.D5
  N9: IC1.In_4, Componente1.D4
  N10: IC1.+V, Componente1.VIN
  N11: Componente2.D9_PWM, J1.pulse
  N12: Componente2.D5_PWM, hc-sr2.Echo
  N13: Componente2.D6_PWM, hc-sr2.Trig
  VCC: Componente2.5V, hc-sr2.VCC, J1.vcc, VCC2.+
  GND: Componente2.GND, hc-sr2.GND, J1.gnd, VCC2.-
